# Fritzing sketch Ambilight (saved by Fritzing 0.9.2b)

parts:
  Part1 = Arduino Nano (Rev3.0)
  LPD8806_RGB_LED_Strip1 = LPD8806 RGB LED Strip
  NEOPIXEL2 = Neopixel Strip -- Black (30/m)
  R1 = Resistor [tolerance=±5% resistance=470 package=THT]
  Pro_Micro2 = Pro Micro
  Part2 = Arduino Nano (Rev3.0)
  LPD8806_RGB_LED_Strip2 = LPD8806 RGB LED Strip
  Pro_Micro3 = Pro Micro
  NEOPIXEL3 = Neopixel Strip -- Black (30/m)
  JACK1 = 2.1mm Barrel Jack with Terminal Block
  JACK2 = 2.1mm Barrel Jack with Terminal Block
  JACK3 = 2.1mm Barrel Jack with Terminal Block
  JACK4 = 2.1mm Barrel Jack with Terminal Block
  R2 = Resistor [tolerance=±5% resistance=470 package=THT]

nets:
  N1: Part1.D11/MOSI, LPD8806_RGB_LED_Strip1.DI
  GND: Part1.GND, LPD8806_RGB_LED_Strip1.GND, JACK1.NEG
  N2: Part1.D13/SCK, LPD8806_RGB_LED_Strip1.CI
  N3: LPD8806_RGB_LED_Strip1.+5V, JACK1.POS
  GND_2: NEOPIXEL2.GND, Part2.GND, JACK2.NEG
  N4: NEOPIXEL2.Din, R1.Pin_1
  N5: NEOPIXEL2.+5V, JACK2.POS
  N6: R1.Pin_0, Part2.D6
  GND_3: Pro_Micro2.GND, LPD8806_RGB_LED_Strip2.GND, JACK3.NEG
  N7: Pro_Micro2.D16/MOSI, LPD8806_RGB_LED_Strip2.DI
  N8: Pro_Micro2.D15/SCLK, LPD8806_RGB_LED_Strip2.CI
  N9: LPD8806_RGB_LED_Strip2.+5V, JACK3.POS
  GND_4: Pro_Micro3.GND, NEOPIXEL3.GND, JACK4.NEG
  N10: NEOPIXEL3.Din, R2.Pin_1
  N11: NEOPIXEL3.+5V, JACK4.POS

custom parts:
  LPD8806 RGB LED Strip: Digitally addressable RGB LED strip
  Neopixel Strip -- Black (30/m): These NeoPixel strips have 30 digitally-addressable pixel LEDs per meter and are very affordable and are only 12.5 mm wide, 10 mm if you remove the strip from the casing.
  Pro Micro: The SparkFun Pro Micro is a complete USB-based microcontoller development system, in a very small footprint, capable of implementing many types of projects. All programming can be done via the USB port.
